// Logisim project Circuito S1eS2.circ as structural Verilog
module s1 (
  input  A,
  input  B,
  output S2,
  output S1
);

  wire and_1_out, and_2_out, and_3_out, and_4_out, not_1_out, not_2_out, not_3_out, not_4_out;

  not not_1 (not_1_out, A);
  and and_1 (and_1_out, not_1_out, B);
  and and_2 (and_2_out, A, not_2_out);
  not not_2 (not_2_out, B);
  not not_3 (not_3_out, A);
  and and_3 (and_3_out, not_3_out, not_4_out);
  not not_4 (not_4_out, B);
  and and_4 (and_4_out, A, B);
  nor nor_1 (S2, and_1_out, and_2_out);
  or or_1 (S1, and_3_out, and_4_out);
endmodule
